// Logisim project Chips.circ as structural Verilog: 4 circuits, main circuit TTTC
module TTTC (
  input  [1:0] vin,
  input  [1:0] hin,
  input  btn,
  output vout,
  output hout,
  output [3:0] L0,
  output [3:0] L1,
  output [3:0] L2,
  output [3:0] L3
);
endmodule

module BPC (
  input  [1:0] H0,
  input  [1:0] H1,
  input  [1:0] H2,
  input  [1:0] V0,
  input  [1:0] V1,
  input  [1:0] V2,
  input  reset,
  output ready,
  output [3:0] XY
);
endmodule

module SDR (
  input  [1:0] symID,
  input  [3:0] XY,
  input  clock,
  output [2:0] H0,
  output [2:0] H1,
  output [2:0] H2,
  output [2:0] V0,
  output [2:0] V1,
  output [2:0] V2
);
endmodule

module GSDD (
  input  [1:0] score,
  input  clock,
  output win,
  output lose,
  output draw
);
endmodule
