// Logisim project Main.circ as structural Verilog: 1 circuit, main circuit Main
module Main (
);

  wire button_1_out, cdm_8_1_p2, cdm_8_1_p4, cdm_8_1_p5, cdm_8_1_p6, cdm_8_1_p7, cdm_8_1_p8, cdm_8_1_p9,
       cdm_8_1_p10, Cl, Code, data, I_Osel, In_out_prime, mem, nand_1_out, not_1_out, not_2_out, RAM;
  wire [3:0] I_Oadr;
  wire [7:0] cdm_8_1_p13, cdm_8_1_p14, cdm_8_1_p15;
  wire [7:4] I_Odat;

  // Probe on cdm_8_1_p2
  // Probe on cdm_8_1_p4
  Button button_1 (.out(button_1_out));
  Clock clock_1 (.out(Cl));
  and and_1 (I_Osel, not_1_out, Cl, data);
  // Probe on cdm_8_1_p7
  // Probe on cdm_8_1_p5
  // Probe on cdm_8_1_p6
  not not_1 (not_1_out, nand_1_out);
  and and_2 (RAM, nand_1_out, data);
  // Probe on cdm_8_1_p9
  // Probe on cdm_8_1_p8
  nand nand_1 (nand_1_out, I_Odat[4], I_Odat[5], I_Odat[6], I_Odat[7]);
  // CdM_8 cdm_8_1: pin names not known; wires that end beside it: Cl, cdm_8_1_p2, button_1_out, cdm_8_1_p4, cdm_8_1_p5, cdm_8_1_p6, cdm_8_1_p7, cdm_8_1_p8, cdm_8_1_p9, cdm_8_1_p10, mem, In_out_prime, cdm_8_1_p13, cdm_8_1_p14, cdm_8_1_p15
  Decoder decoder_1 (.out0(Code), .out1(data), .sel(cdm_8_1_p10), .en(mem));
  assign {I_Odat, I_Oadr} = not_2_out ? cdm_8_1_p14 : 8'bz;  // Controlled_Buffer controlled_buffer_1
  not not_2 (not_2_out, In_out_prime);
  assign cdm_8_1_p15 = In_out_prime ? {I_Odat, I_Oadr} : 8'bz;  // Controlled_Buffer controlled_buffer_2
  Pull_Resistor pull_resistor_1 (.node(I_Oadr[0]));
  Pull_Resistor pull_resistor_2 (.node(I_Oadr[1]));
  Pull_Resistor pull_resistor_3 (.node(I_Oadr[2]));
  Pull_Resistor pull_resistor_4 (.node(I_Oadr[3]));
  Pull_Resistor pull_resistor_5 (.node(I_Odat[4]));
  Pull_Resistor pull_resistor_6 (.node(I_Odat[5]));
  Pull_Resistor pull_resistor_7 (.node(I_Odat[6]));
  Pull_Resistor pull_resistor_8 (.node(I_Odat[7]));
  ROM rom_1 (.addr(cdm_8_1_p13), .data({I_Odat, I_Oadr}), .sel(Code));
  RAM ram_1 (.addr(cdm_8_1_p13), .data({I_Odat, I_Oadr}), .sel(RAM), .clk(Cl), .ld(In_out_prime));  // open: clr

  // Other names for the same wires on the sheet: I_Odat[3:0] = I_Oadr; rd_wr_prime = In_out_prime

  // Notes on the sheet:
  //   THE BUS
endmodule
